// Logisim project logic_ckt_01.circ as structural Verilog: 1 circuit, main circuit main
module main (
  output out_1,
  output out_2,
  output out_3,
  output out_4,
  output out_5,
  output out_6,
  output out_7,
  output out_8
);

  wire multiplexer_1_out, multiplexer_2_out, multiplexer_3_out, multiplexer_4_out, multiplexer_5_out,
       multiplexer_6_out, multiplexer_7_out, multiplexer_8_out;

  Priority_Encoder priority_encoder_1 (
    .in0(1'b0), .in1(1'b0), .in2(1'b0), .in3(1'b0), .in4(1'b0), .in5(1'b0), .in6(1'b0), .in7(1'b0),
    .out({out_3, out_2, out_1}));  // open: en_in, gs, en_out
  Multiplexer #(.select(3)) multiplexer_1 (
    .in0(1'b1), .in1(1'b1), .in2(1'b1), .in3(1'b1), .in4(1'b1), .in5(1'b0), .in6(1'b1), .in7(1'b1),
    .out(multiplexer_1_out), .sel(3'b011));  // open: en
  or or_1 (out_6, 1'b0, 1'b0, 1'b0, 1'b0);
  or or_2 (out_7, 1'b0, 1'b0, 1'b0, 1'b0);
  or or_3 (out_8, 1'b0, 1'b0, 1'b0, 1'b0);
  LED led_1 (.in(multiplexer_1_out));
  Multiplexer multiplexer_2 (.in0(1'b0), .in1(1'b0), .out(multiplexer_2_out), .sel(1'b1));  // open: en
  Multiplexer multiplexer_3 (.in0(1'b0), .in1(1'b0), .out(multiplexer_3_out), .sel(1'b1));  // open: en
  Multiplexer multiplexer_4 (.in0(1'b0), .in1(1'b0), .out(multiplexer_4_out), .sel(1'b1));  // open: en
  Multiplexer multiplexer_5 (.in0(1'b0), .in1(1'b0), .out(multiplexer_5_out), .sel(1'b1));  // open: en
  or or_4 (out_4, 1'b0, 1'b0);
  or or_5 (out_5, 1'b0, 1'b0);
  Multiplexer multiplexer_6 (
    .in0(multiplexer_2_out), .in1(multiplexer_3_out), .out(multiplexer_6_out), .sel(1'b1));  // open: en
  Multiplexer multiplexer_7 (
    .in0(multiplexer_4_out), .in1(multiplexer_5_out), .out(multiplexer_7_out), .sel(1'b0));  // open: en
  Multiplexer multiplexer_8 (
    .in0(multiplexer_6_out), .in1(multiplexer_7_out), .out(multiplexer_8_out), .sel(1'b1));  // open: en
  LED led_2 (.in(multiplexer_8_out));
endmodule
